// Logisim project CPU.circ as structural Verilog: 1 circuit, main circuit main
module main (
);

  wire and_1_out, and_2_out, and_3_out, and_4_out, button_1_out, clock_1_out, decoder_1_out0, decoder_1_out1,
       decoder_1_out2, decoder_1_out3, not_1_out, or_1_out, RegWrite_out;
  wire [3:0] multiplexer_1_out, multiplexer_1_out_2, R2_q, R2_q_2, R3_q, R3_q_2;
  wire [7:0] adder_1_out, adder_2_out, DRAM_dout, Instruction_Memory_dout, multiplexer_2_out,
       multiplexer_3_out, multiplexer_4_out, multiplier_1_out, PC_q, R0_q, R1_q;

  Clock clock_1 (.out(clock_1_out));
  Button button_1 (.out(button_1_out));
  or or_1 (or_1_out, clock_1_out, button_1_out);
  and RegWrite (RegWrite_out, Instruction_Memory_dout[6], Instruction_Memory_dout[7]);
  Decoder #(.select(2)) decoder_1 (
    .out0(decoder_1_out0), .out1(decoder_1_out1), .out2(decoder_1_out2), .out3(decoder_1_out3),
    .sel(Instruction_Memory_dout[5:4]));  // open: en
  not not_1 (not_1_out, RegWrite_out);
  LED led_1 (.in(not_1_out));
  Adder adder_1 (.a(PC_q), .b(8'h1), .out(adder_1_out));  // open: cin, cout
  RAM #(.enables("line")) Instruction_Memory (
    .addr(PC_q), .clk(or_1_out), .dout(Instruction_Memory_dout));  // open: we, din
  and and_1 (and_1_out, not_1_out, decoder_1_out0);
  and and_2 (and_2_out, not_1_out, decoder_1_out1);
  and and_3 (and_3_out, not_1_out, decoder_1_out2);
  and and_4 (and_4_out, not_1_out, decoder_1_out3);
  Register PC (.D(adder_1_out), .clk(or_1_out), .Q(PC_q));  // open: en, clr
  Adder adder_2 (.a(multiplexer_4_out), .b(multiplexer_3_out), .out(adder_2_out));  // open: cin, cout
  Hex_Digit_Display #(.decimalPoint("false")) Write (.value(multiplexer_1_out_2));
  Hex_Digit_Display #(.decimalPoint("false")) Data (.value(multiplexer_1_out));
  Hex_Digit_Display #(.decimalPoint("false")) Program (.value(PC_q[7:4]));
  Multiplexer #(.width(8)) multiplexer_1 (
    .in0(multiplexer_2_out), .in1(DRAM_dout), .out({multiplexer_1_out_2, multiplexer_1_out}),
    .sel(Instruction_Memory_dout[7]));
  Hex_Digit_Display #(.decimalPoint("false")) Counter (.value(PC_q[3:0]));
  Hex_Digit_Display #(.decimalPoint("false")) Instru (.value(Instruction_Memory_dout[7:4]));
  Multiplier multiplier_1 (.a(multiplexer_4_out), .b(multiplexer_3_out), .out(multiplier_1_out));  // open: cin, cout
  Multiplexer #(.width(8)) multiplexer_2 (
    .in0(adder_2_out), .in1(multiplier_1_out), .out(multiplexer_2_out), .sel(Instruction_Memory_dout[6]));
  Hex_Digit_Display #(.decimalPoint("false")) ction (.value(Instruction_Memory_dout[3:0]));
  Register R0 (.D({multiplexer_1_out_2, multiplexer_1_out}), .en(and_1_out), .clk(or_1_out), .Q(R0_q));  // open: clr
  LED led_2 (.in(and_1_out));
  Register R1 (.D({multiplexer_1_out_2, multiplexer_1_out}), .en(and_2_out), .clk(or_1_out), .Q(R1_q));  // open: clr
  LED led_3 (.in(and_2_out));
  Register R2 (
    .D({multiplexer_1_out_2, multiplexer_1_out}), .en(and_3_out), .clk(or_1_out), .Q({R2_q_2, R2_q}));  // open: clr
  LED led_4 (.in(and_3_out));
  Register R3 (
    .D({multiplexer_1_out_2, multiplexer_1_out}), .en(and_4_out), .clk(or_1_out), .Q({R3_q_2, R3_q}));  // open: clr
  LED led_5 (.in(and_4_out));
  RAM #(.addrWidth(4), .enables("line")) DRAM (
    .addr(Instruction_Memory_dout[3:0]), .we(RegWrite_out), .clk(or_1_out), .din(multiplexer_4_out),
    .dout(DRAM_dout));
  LED MemWrite (.in(RegWrite_out));
  Multiplexer #(.select(2), .width(8)) multiplexer_3 (
    .in0(R0_q), .in1(R1_q), .in2({R2_q_2, R2_q}), .in3({R3_q_2, R3_q}), .out(multiplexer_3_out),
    .sel(Instruction_Memory_dout[1:0]));
  Multiplexer #(.select(2), .width(8)) multiplexer_4 (
    .in0(R0_q), .in1(R1_q), .in2({R2_q_2, R2_q}), .in3({R3_q_2, R3_q}), .out(multiplexer_4_out),
    .sel(Instruction_Memory_dout[3:2]));
  Hex_Digit_Display #(.decimalPoint("false")) Reg0 (.value(R0_q[7:4]));
  Hex_Digit_Display #(.decimalPoint("false")) hex_digit_display_1 (.value(R0_q[3:0]));
  Hex_Digit_Display #(.decimalPoint("false")) hex_digit_display_2 (.value(multiplexer_4_out[7:4]));
  Hex_Digit_Display #(.decimalPoint("false")) RegData1 (.value(multiplexer_4_out[3:0]));
  Hex_Digit_Display #(.decimalPoint("false")) hex_digit_display_3 (.value(multiplexer_3_out[7:4]));
  Hex_Digit_Display #(.decimalPoint("false")) RegData2 (.value(multiplexer_3_out[3:0]));
  Hex_Digit_Display #(.decimalPoint("false")) DR (.value(DRAM_dout[7:4]));
  Hex_Digit_Display #(.decimalPoint("false")) AM (.value(DRAM_dout[3:0]));
  Hex_Digit_Display #(.decimalPoint("false")) hex_digit_display_4 (.value(R1_q[3:0]));
  Hex_Digit_Display #(.decimalPoint("false")) Reg1 (.value(R1_q[7:4]));
  Hex_Digit_Display #(.decimalPoint("false")) Reg2 (.value(R2_q_2));
  Hex_Digit_Display #(.decimalPoint("false")) hex_digit_display_5 (.value(R2_q));
  Hex_Digit_Display #(.decimalPoint("false")) Reg3 (.value(R3_q_2));
  Hex_Digit_Display #(.decimalPoint("false")) hex_digit_display_6 (.value(R3_q));

  // Notes on the sheet:
  //   Press me to
  //   step the clock!
  //   Andrew Schomber
  //   Matthew Bernardon
  //   CPU Name: x80Hao
  //   I pledge my honor that I have abided by the Stevens Honor System.
endmodule
